// Logisim project CounterParallel.circ as structural Verilog: 1 circuit, main circuit main
module main (
);

  wire and_1_out, and_2_out, clock_1_out, t_ff_1_q, t_ff_1_qn, t_ff_2_qn, t_ff_3_q, t_ff_3_qn, t_ff_4_q,
       t_ff_4_qn, t_ff_5_q, t_ff_6_qn, t_ff_7_q, t_ff_7_qn;

  Clock clock_1 (.out(clock_1_out));
  T_Flip_Flop t_ff_1 (.T(1'b1), .clk(t_ff_7_qn), .Q(t_ff_1_q), .Qn(t_ff_1_qn), .reset(and_1_out));  // open: preset
  T_Flip_Flop t_ff_2 (.T(1'b1), .clk(clock_1_out), .Qn(t_ff_2_qn), .reset(and_2_out));  // open: Q, preset
  T_Flip_Flop t_ff_3 (.T(1'b1), .clk(t_ff_1_qn), .Q(t_ff_3_q), .Qn(t_ff_3_qn), .reset(and_1_out));  // open: preset
  and and_1 (and_1_out, t_ff_1_q, t_ff_5_q);
  T_Flip_Flop t_ff_4 (.T(1'b1), .clk(t_ff_2_qn), .Q(t_ff_4_q), .Qn(t_ff_4_qn), .reset(and_2_out));  // open: preset
  T_Flip_Flop t_ff_5 (.T(1'b1), .clk(t_ff_3_qn), .Q(t_ff_5_q), .reset(and_1_out));  // open: Qn, preset
  T_Flip_Flop t_ff_6 (.T(1'b1), .clk(t_ff_4_qn), .Qn(t_ff_6_qn), .reset(and_2_out));  // open: Q, preset
  and and_2 (and_2_out, t_ff_4_q, t_ff_7_q);
  T_Flip_Flop t_ff_7 (.T(1'b1), .clk(t_ff_6_qn), .Q(t_ff_7_q), .Qn(t_ff_7_qn), .reset(and_2_out));  // open: preset
endmodule
