// Logisim project Lab1.circ as structural Verilog: 1 circuit, main circuit main
module main (
);

  wire and_1_out, and_2_out, and_3_out, clock_1_out, J0_out, J1_out, J2_out, K0_out, K1_out, K3_out,
       not_1_out, not_2_out, not_3_out, not_4_out, not_5_out, not_6_out, not_7_out, Q0_q, Q1_q, Q2_q, Q3_q;

  Clock clock_1 (.out(clock_1_out));
  not not_1 (not_1_out, Q2_q);
  not not_2 (not_2_out, Q1_q);
  not not_3 (not_3_out, Q2_q);
  not not_4 (not_4_out, Q3_q);
  not not_5 (not_5_out, Q0_q);
  not not_6 (not_6_out, Q2_q);
  J_K_Flip_Flop #(.trigger("falling")) Q0 (
    .J(J0_out), .K(K0_out), .clk(clock_1_out), .Q(Q0_q));  // open: Qn, preset, reset
  and J0 (J0_out, Q1_q, not_1_out, Q3_q);
  and and_1 (and_1_out, not_2_out, not_4_out);
  and and_2 (and_2_out, not_5_out, Q2_q, Q3_q);
  and and_3 (and_3_out, Q0_q, not_6_out, Q3_q);
  not not_7 (not_7_out, Q1_q);
  or K0 (K0_out, J0_out, Q2_q, and_1_out);
  or J1 (J1_out, and_2_out, and_3_out);
  or K1 (K1_out, not_5_out, Q2_q, Q3_q);
  and J2 (J2_out, not_5_out, not_7_out, Q3_q);
  and K3 (K3_out, Q0_q, not_7_out, not_3_out);
  J_K_Flip_Flop #(.trigger("falling")) Q1 (
    .J(J1_out), .K(K1_out), .clk(clock_1_out), .Q(Q1_q));  // open: Qn, preset, reset
  J_K_Flip_Flop #(.trigger("falling")) Q2 (
    .J(J2_out), .K(1'b1), .clk(clock_1_out), .Q(Q2_q));  // open: Qn, preset, reset
  J_K_Flip_Flop #(.trigger("falling")) Q3 (
    .J(1'b1), .K(K3_out), .clk(clock_1_out), .Q(Q3_q));  // open: Qn, preset, reset
endmodule
