// Logisim project SincyCounter.circ as structural Verilog: 1 circuit, main circuit main
module main (
);

  wire and_1_out, and_2_out, and_3_out, clock_1_out, clock_2_out, clock_3_out, or_1_out, or_2_out, or_3_out,
       Q0_q, Q1_q, Q1_qn, Q2_q, Q2_qn, t_ff_1_q, t_ff_2_q, t_ff_3_q, t_ff_4_q, t_ff_5_q, t_ff_6_q, t_ff_7_q;

  Clock clock_1 (.out(clock_1_out));
  T_Flip_Flop #(.trigger("falling")) t_ff_1 (
    .T(1'b1), .clk(clock_1_out), .Q(t_ff_1_q), .reset(and_1_out));  // open: Qn, preset
  buf and_1 (and_1_out, t_ff_4_q);  // AND_Gate
  Clock clock_2 (.out(clock_2_out));
  T_Flip_Flop #(.trigger("falling")) t_ff_2 (
    .T(1'b1), .clk(t_ff_1_q), .Q(t_ff_2_q), .reset(and_1_out));  // open: Qn, preset
  T_Flip_Flop #(.trigger("falling")) t_ff_3 (.T(1'b1), .clk(clock_2_out), .Q(t_ff_3_q));  // open: Qn, reset, preset
  Clock clock_3 (.out(clock_3_out));
  T_Flip_Flop #(.trigger("falling")) t_ff_4 (
    .T(1'b1), .clk(t_ff_2_q), .Q(t_ff_4_q), .reset(and_1_out));  // open: Qn, preset
  J_K_Flip_Flop #(.trigger("falling")) Q0 (
    .J(or_3_out), .K(1'b1), .clk(clock_3_out), .Q(Q0_q));  // open: Qn, preset, reset
  and and_2 (and_2_out, Q0_q, Q2_qn);
  or or_1 (or_1_out, Q0_q, Q2_q);
  T_Flip_Flop #(.trigger("falling")) t_ff_5 (.T(1'b1), .clk(t_ff_3_q), .Q(t_ff_5_q));  // open: Qn, reset, preset
  T_Flip_Flop #(.trigger("falling")) t_ff_6 (.T(1'b1), .clk(t_ff_5_q), .Q(t_ff_6_q));  // open: Qn, reset, preset
  J_K_Flip_Flop #(.trigger("falling")) Q1 (
    .J(and_2_out), .K(or_1_out), .clk(clock_3_out), .Q(Q1_q), .Qn(Q1_qn));  // open: preset, reset
  or or_2 (or_2_out, Q1_q, Q0_q);
  and and_3 (and_3_out, Q0_q, Q1_q);
  T_Flip_Flop #(.trigger("falling")) t_ff_7 (.T(1'b1), .clk(t_ff_6_q), .Q(t_ff_7_q));  // open: Qn, reset, preset
  J_K_Flip_Flop #(.trigger("falling")) Q2 (
    .J(and_3_out), .K(or_2_out), .clk(clock_3_out), .Q(Q2_q), .Qn(Q2_qn));  // open: preset, reset
  or or_3 (or_3_out, Q2_qn, Q1_qn);
  LED led_1 (.in(t_ff_7_q));
  LED led_2 (.in(clock_2_out));
endmodule
