// Logisim project Study.circ as structural Verilog: 1 circuit, main circuit main
module main (
);

  wire and_1_out, clock_1_out, clock_2_out, t_ff_1_q, t_ff_2_q, t_ff_3_q, t_ff_4_q, t_ff_5_q, t_ff_6_q,
       t_ff_7_q, t_ff_8_q;

  Clock clock_1 (.out(clock_1_out));
  Clock clock_2 (.out(clock_2_out));
  and and_1 (and_1_out, t_ff_2_q, t_ff_4_q, t_ff_6_q, t_ff_8_q);
  T_Flip_Flop #(.trigger("falling")) t_ff_1 (.T(1'b1), .clk(clock_1_out), .Q(t_ff_1_q));  // open: Qn, reset, preset
  T_Flip_Flop #(.trigger("falling")) t_ff_2 (
    .T(1'b1), .clk(clock_2_out), .Q(t_ff_2_q), .reset(and_1_out));  // open: Qn, preset
  T_Flip_Flop #(.trigger("falling")) t_ff_3 (.T(1'b1), .clk(t_ff_1_q), .Q(t_ff_3_q));  // open: Qn, reset, preset
  T_Flip_Flop #(.trigger("falling")) t_ff_4 (
    .T(1'b1), .clk(t_ff_2_q), .Q(t_ff_4_q), .reset(and_1_out));  // open: Qn, preset
  T_Flip_Flop #(.trigger("falling")) t_ff_5 (.T(1'b1), .clk(t_ff_3_q), .Q(t_ff_5_q));  // open: Qn, reset, preset
  T_Flip_Flop #(.trigger("falling")) t_ff_6 (
    .T(1'b1), .clk(t_ff_4_q), .Q(t_ff_6_q), .reset(and_1_out));  // open: Qn, preset
  T_Flip_Flop #(.trigger("falling")) t_ff_7 (.T(1'b1), .clk(t_ff_5_q), .Q(t_ff_7_q));  // open: Qn, reset, preset
  T_Flip_Flop #(.trigger("falling")) t_ff_8 (
    .T(1'b1), .clk(t_ff_6_q), .Q(t_ff_8_q), .reset(and_1_out));  // open: Qn, preset
  LED led_1 (.in(t_ff_7_q));
  LED led_2 (.in(clock_1_out));
  LED led_3 (.in(t_ff_8_q));
  LED led_4 (.in(clock_2_out));
endmodule
